// Logisim project CPU.circ as structural Verilog: 1 circuit, main circuit main
// CPU
module main (
  input  [31:0] INSTRUCTION,
  input  [23:0] CURRENT_PC,
  input  CQ_PASSED,
  input  [31:0] REG_1_VAL,
  input  [31:0] REG_2_VAL,
  input  [31:0] REG_3_VAL,
  input  [31:0] ALU_RESULT,
  input  [31:0] MEM_OUT,
  output [23:0] JUMP_ADDRESS,
  output [2:0] CQ_QUERY,
  output CR_WRITE,
  output [3:0] REG_1_READ,
  output [3:0] REG_2_READ,
  output [3:0] REG_3_WRITE,
  output [31:0] REG_WRITE_VAL,
  output REG_WRITE,
  output [31:0] ALU_SOURCE_X,
  output [31:0] ALU_SOURCE_Y,
  output [3:0] ALU_OPERATION,
  output [23:0] MEM_ADDR,
  output [31:0] MEM_IN,
  output MEM_WRITE
);


  // Notes on the sheet:
  //   INSTRUCTION MODULE
  //   CR MODULE
  //   REGISTER FILE MODULE
  //   ALU MODULE
  //   MEMORY MODULE
endmodule
