// Logisim project REG.circ as structural Verilog: 1 circuit, main circuit main
// REG
module main (
  input  CLOCK,
  input  [3:0] REG_1_READ,
  input  [3:0] REG_2_READ,
  input  [3:0] REG_3_WRITE,
  input  [31:0] REG_WRITE_VAL,
  input  REG_WRITE,
  output [31:0] R00,
  output [31:0] R01,
  output [31:0] R02,
  output [31:0] R03,
  output [31:0] R04,
  output [31:0] R05,
  output [31:0] R06,
  output [31:0] R07,
  output [31:0] REG_1_VAL,
  output [31:0] REG_2_VAL,
  output [31:0] REG_3_VAL,
  output [31:0] R08,
  output [31:0] R09,
  output [31:0] R10,
  output [31:0] R11,
  output [31:0] R12,
  output [31:0] R13,
  output [31:0] R14,
  output [31:0] R15
);


  // Notes on the sheet:
  //   REGISTER FILE MODULE
endmodule
